# Fritzing sketch Arduino to Arduino MIDI (saved by Fritzing 0.7.0b)

parts:
  Arduino1 = Arduino
  Arduino2 = Arduino
  LED1 = LED - 5mm [color="Red (633nm)" package="5 mm [THT]"]

nets:
  GND: Arduino1.GND, Arduino2.GND, LED1.cathode
  N1: Arduino1.D1TX, Arduino2.D0RX
  N2: Arduino2.D9, LED1.anode
