# Fritzing sketch Transistor Motor (saved by Fritzing 0.8.7b)
circuit board: 4.99721cm x 5.36502cm
breadboards: 1

parts:
  Arduino = Arduino Uno (Rev3)
  R1 = Resistor [tolerance=±5% resistance=220 package=THT]
  D2 = Rectifier Diode [part_number=1N4001 package="300 mil [THT]"]
  M3 = DC Motor
  Q1 = NPN-Transistor [package="TO92 [THT]"]

nets:
  N1: Arduino.D9_PWM, R1.Pin_1
  N2: Arduino.GND, Q1.C
  N3: Arduino.5V, D2.cathode, M3.pin_1
  N4: R1.Pin_0, Q1.B
  N5: D2.anode, M3.pin_2, Q1.E
