# Fritzing sketch ZweiUndZwei (saved by Fritzing 0.7.4b)

parts:
  Arduino1 = Arduino
  Arduino2 = Arduino

nets:
  GND: Arduino1.GND, Arduino2.GND
  N1: Arduino1.D1TX, Arduino2.D0RX
  N2: Arduino1.D0RX, Arduino2.D1TX
  +5V: Arduino1.+5V, Arduino2.+5V
